# Fritzing sketch wiring (saved by Fritzing 0.9.0b)

parts:
  Raspberry_Pi_B_rev1 = Raspberry Pi B rev2
  SVert = Pushbutton [package="[THT]"]
  SRouge = Pushbutton [package="[THT]"]
  LCD1 = LCD screen  # not connected
  Tiny_RTC1 = Tiny RTC

nets:
  N1: Raspberry_Pi_B_rev1.GPIO_2, Tiny_RTC1.SDA#8
  N2: Raspberry_Pi_B_rev1.GPIO_3, Tiny_RTC1.SCL#7
  N3: Raspberry_Pi_B_rev1.GND, SVert.Pin_4, SRouge.Pin_1, SRouge.Pin_2, Tiny_RTC1.GND#10
  N4: Raspberry_Pi_B_rev1.GPIO_23, SVert.Pin_2
  N5: Raspberry_Pi_B_rev1.GPIO_24, SRouge.Pin_3, SRouge.Pin_4
  N6: Raspberry_Pi_B_rev1.5V, Tiny_RTC1.VCC#9

notes:
  GND
  VCC
  SDA
  SCL
  Green
  Red

custom parts:
  Tiny RTC: Tiny RTC I2C module DS1370Z RTC and AT24C32 EEPROM
